// Logisim project Mini Project final diag.circ as structural Verilog: 1 circuit, main circuit main
module main (
  input  [7:0] TEMP_READING,
  input  [7:0] MAX_TEMP,
  input  [11:0] PULSE_READING,
  input  [11:0] MIN_PULSE_RATE,
  input  [11:0] MAX_PULSE_RATE,
  input  [7:0] SPO2_LEVEL,
  input  [7:0] MIN_SPO2_LEVEL,
  input  [7:0] in_8,
  input  [7:0] in_9,
  input  [7:0] in_10,
  input  [7:0] in_11,
  input  [7:0] in_12,
  input  [7:0] in_13,
  output [7:0] _18
);

  wire AND_2_out, AND_3_out, AND_4_out, AND_5_out, AND_6_out, AND_7_out, AND_8_out, AND_9_out, AND_out,
       comparator_1_gt, comparator_2_lt, comparator_3_gt, comparator_4_gt, decoder_1_out0, decoder_1_out1,
       decoder_1_out2, decoder_1_out3, decoder_1_out4, decoder_1_out5, decoder_1_out6, decoder_1_out7,
       decoder_2_out0, decoder_2_out1, decoder_2_out2, decoder_2_out3, decoder_2_out4, decoder_2_out5,
       decoder_2_out6, decoder_2_out7, NOT_2_out, NOT_3_out, NOT_4_out, NOT_out, OR_2_out, OR_out,
       subtractor_1_bout;
  wire [7:0] multiplexer_1_out, multiplexer_2_out, multiplexer_3_out, subtractor_1_out, XOR_out;

  Comparator comparator_1 (.a(TEMP_READING), .b(MAX_TEMP), .gt(comparator_1_gt));  // open: eq, lt
  Comparator #(.width(12)) comparator_2 (.a(PULSE_READING), .b(MIN_PULSE_RATE), .lt(comparator_2_lt));  // open: gt, eq
  Comparator #(.width(12)) comparator_3 (.a(PULSE_READING), .b(MAX_PULSE_RATE), .gt(comparator_3_gt));  // open: eq, lt
  Subtractor subtractor_1 (
    .a(SPO2_LEVEL), .b(MIN_SPO2_LEVEL), .out(subtractor_1_out), .bout(subtractor_1_bout));  // open: bin
  Multiplexer #(.width(8)) multiplexer_1 (
    .in0(in_8), .in1(in_10), .out(multiplexer_1_out), .sel(subtractor_1_bout));  // open: en
  or OR (OR_out, comparator_2_lt, comparator_3_gt);
  assign XOR_out = subtractor_1_out ^ multiplexer_1_out;  // XOR_Gate XOR, 8 bits wide
  Multiplexer #(.width(8)) multiplexer_2 (
    .in0(in_11), .in1(in_13), .out(multiplexer_2_out), .sel(subtractor_1_bout));  // open: en
  Adder adder_1 (.a(XOR_out), .b(multiplexer_2_out), .out(_18));  // open: cin, cout
  Multiplexer #(.width(8)) multiplexer_3 (
    .in0(in_12), .in1(_18), .out(multiplexer_3_out), .sel(subtractor_1_bout));  // open: en
  Comparator comparator_4 (.a(_18), .b(in_9), .gt(comparator_4_gt));  // open: eq, lt
  Decoder #(.select(3)) decoder_1 (
    .out0(decoder_1_out0), .out1(decoder_1_out1), .out2(decoder_1_out2), .out3(decoder_1_out3),
    .out4(decoder_1_out4), .out5(decoder_1_out5), .out6(decoder_1_out6), .out7(decoder_1_out7),
    .sel(multiplexer_3_out[6:4]));  // open: en
  not NOT (NOT_out, multiplexer_3_out[7]);
  not NOT_2 (NOT_2_out, decoder_1_out1);
  and AND (AND_out, comparator_1_gt, OR_out);
  and AND_2 (AND_2_out, OR_out, comparator_4_gt);
  and AND_3 (AND_3_out, comparator_1_gt, comparator_4_gt);
  or OR_2 (OR_2_out, AND_3_out, AND_2_out, AND_out);
  LED led_1 (.in(decoder_1_out0));
  and AND_4 (AND_4_out, decoder_1_out1, NOT_out);
  LED led_2 (.in(AND_4_out));
  LED led_3 (.in(decoder_1_out2));
  LED led_4 (.in(decoder_1_out3));
  LED led_5 (.in(decoder_1_out4));
  LED led_6 (.in(decoder_1_out5));
  LED led_7 (.in(decoder_1_out6));
  LED led_8 (.in(decoder_1_out7));
  LED led_9 (.in(AND_5_out));
  and AND_5 (AND_5_out, NOT_2_out, multiplexer_3_out[7]);
  LED led_10 (.in(AND_6_out));
  and AND_6 (AND_6_out, decoder_1_out1, multiplexer_3_out[7]);
  Decoder #(.select(3)) decoder_2 (
    .out0(decoder_2_out0), .out1(decoder_2_out1), .out2(decoder_2_out2), .out3(decoder_2_out3),
    .out4(decoder_2_out4), .out5(decoder_2_out5), .out6(decoder_2_out6), .out7(decoder_2_out7),
    .sel(multiplexer_3_out[2:0]));  // open: en
  LED led_11 (.in(OR_2_out));
  not NOT_3 (NOT_3_out, multiplexer_3_out[3]);
  not NOT_4 (NOT_4_out, decoder_2_out1);
  LED led_12 (.in(decoder_2_out0));
  and AND_7 (AND_7_out, decoder_2_out1, NOT_3_out);
  LED led_13 (.in(AND_7_out));
  LED led_14 (.in(decoder_2_out2));
  LED led_15 (.in(decoder_2_out3));
  LED led_16 (.in(decoder_2_out4));
  LED led_17 (.in(decoder_2_out5));
  LED led_18 (.in(decoder_2_out6));
  LED led_19 (.in(decoder_2_out7));
  and AND_8 (AND_8_out, NOT_4_out, multiplexer_3_out[3]);
  LED led_20 (.in(AND_8_out));
  and AND_9 (AND_9_out, decoder_2_out1, multiplexer_3_out[3]);
  LED led_21 (.in(AND_9_out));

  // Notes on the sheet:
  //   60 BPM
  //   100 BPM
  //   95%
  //   37 C
  //   INPUTS(FROM SENSORS) :
  //   INPUTS(FIXED) :
  //   OUTPUT :
  //   COMPONENTS :
  //   SPO2 LEVEL
  //   MIN SPO2 LEVEL
  //   EMERGENCY
  //   1 8-BIT ADDER
  //   2 OR GATES 
  //   9 AND GATES 
  //   1 XOR GATES 
  //   2 NOT GATES 
  //   21 LEDS
  //   COMPARATOR C1
  //   COMPARATOR C2
  //   COMPARATOR C3
  //   TEMPERATURE  READING 
  //   PULSE READING 
  //   (in %)
  //   MAX TEMPERATURE 
  //   MAX PULSE RATE  
  //   MIN PULSE RATE  
  //   4 8-BIT COMPARATOR
  //   1 8-BIT SUBTRACTOR
  //   3 8-BIT MULTIPLEXER
  //   2 3 TO 7 LINE DECODER
  //   SUBTRACTOR
  //   M1
  //   (in C)
  //   (in BPM)
  //   OXYGEN SUPPLY GIVEN (TENS DIGIT AND ONES DIGIT)
  //   CIRCUIT DIAGRAM OF RING WITH BODY VITALS SENSORS
  //   M2
  //   ADDER
  //   M3
  //   MAX O2 DIFFERENCE
  //   SPLITER 
  //   COMPARATOR C4
  //   TENS DIGIT 
  //   0
  //   1
  //   2
  //   3
  //   4
  //   5
  //   6
  //   7
  //   8
  //   9
  //   ONES DIGIT 
  //   EMERGENCY
  //   0
  //   1
  //   2
  //   3
  //   4
  //   5
  //   6
  //   7
  //   8
  //   9
endmodule
