// Logisim project 8-bit comparator.circ as structural Verilog: 1 circuit, main circuit main
module main (
  input  A7,
  input  B7,
  input  A6,
  input  B6,
  input  A5,
  input  B5,
  input  A4,
  input  B4,
  input  A3,
  input  B3,
  input  A2,
  input  B2,
  input  A1,
  input  B1,
  input  A0,
  input  B0,
  output OUTPUT
);

  wire and_1_out, and_2_out, and_3_out, and_4_out, and_5_out, and_6_out, and_7_out, multiplexer_1_out,
       multiplexer_2_out, multiplexer_3_out, multiplexer_4_out, multiplexer_5_out, multiplexer_6_out,
       multiplexer_7_out, multiplexer_8_out, multiplexer_9_out, multiplexer_10_out, not_1_out, not_2_out,
       not_3_out, not_4_out, not_5_out, not_6_out, not_7_out, not_8_out, or_1_out, or_2_out, or_3_out,
       or_4_out, or_5_out, or_6_out, or_7_out, or_8_out;

  not not_1 (not_1_out, B7);
  not not_2 (not_2_out, B6);
  not not_3 (not_3_out, B5);
  not not_4 (not_4_out, B4);
  not not_5 (not_5_out, B3);
  not not_6 (not_6_out, B2);
  not not_7 (not_7_out, B1);
  not not_8 (not_8_out, A0);
  or or_1 (or_1_out, A7, not_1_out);
  and and_1 (and_1_out, A7, not_1_out);
  or or_2 (or_2_out, A6, not_2_out);
  and and_2 (and_2_out, A6, not_2_out);
  or or_3 (or_3_out, A5, not_3_out);
  and and_3 (and_3_out, A5, not_3_out);
  or or_4 (or_4_out, A4, not_4_out);
  and and_4 (and_4_out, A4, not_4_out);
  or or_5 (or_5_out, A3, not_5_out);
  and and_5 (and_5_out, A3, not_5_out);
  or or_6 (or_6_out, A2, not_6_out);
  and and_6 (and_6_out, A2, not_6_out);
  or or_7 (or_7_out, A1, not_7_out);
  and and_7 (and_7_out, A1, not_7_out);
  or or_8 (or_8_out, not_8_out, B0);
  Multiplexer multiplexer_1 (.in0(or_1_out), .in1(and_1_out), .out(multiplexer_1_out), .sel(or_2_out));  // open: en
  Multiplexer multiplexer_2 (.in0(or_1_out), .in1(and_1_out), .out(multiplexer_2_out), .sel(and_2_out));  // open: en
  Multiplexer multiplexer_3 (.in0(or_3_out), .in1(and_3_out), .out(multiplexer_3_out), .sel(or_4_out));  // open: en
  Multiplexer multiplexer_4 (.in0(or_3_out), .in1(and_3_out), .out(multiplexer_4_out), .sel(and_4_out));  // open: en
  Multiplexer multiplexer_5 (.in0(or_5_out), .in1(and_5_out), .out(multiplexer_5_out), .sel(or_6_out));  // open: en
  Multiplexer multiplexer_6 (.in0(or_5_out), .in1(and_5_out), .out(multiplexer_6_out), .sel(and_6_out));  // open: en
  Multiplexer multiplexer_7 (.in0(or_7_out), .in1(and_7_out), .out(multiplexer_7_out), .sel(or_8_out));  // open: en
  Multiplexer multiplexer_8 (
    .in0(multiplexer_1_out), .in1(multiplexer_2_out), .out(multiplexer_8_out), .sel(multiplexer_3_out));  // open: en
  Multiplexer multiplexer_9 (
    .in0(multiplexer_1_out), .in1(multiplexer_2_out), .out(multiplexer_9_out), .sel(multiplexer_4_out));  // open: en
  Multiplexer multiplexer_10 (
    .in0(multiplexer_5_out), .in1(multiplexer_6_out), .out(multiplexer_10_out), .sel(multiplexer_7_out));  // open: en
  Multiplexer multiplexer_11 (
    .in0(multiplexer_8_out), .in1(multiplexer_9_out), .out(OUTPUT), .sel(multiplexer_10_out));  // open: en

  // Notes on the sheet:
  //   IF OUTPUT
  //   8 bit Comparator
  //   0  =  LESSER THAN
  //   1  =  GREATER THAN
endmodule
